# Fritzing sketch LedTrialShieldBlueBelt (saved by Fritzing 0.8.7b)
circuit board: 8cm x 10cm
breadboards: 2

parts:
  ArduinoKid = Arduino Uno (Rev3)
  C1 = Electrolytic Capacitor [capacitance=1mF package="100 mil [THT, electrolytic]"]
  LED1 = LED - 5mm [color="Red (633nm)" package="5 mm [THT]"]
  R1 = Resistor [tolerance=±5% resistance=1k package=THT]
  A2 = atmega328 [package=dip]
  C3 = Capacitor [package=cap-pth-small2]
  C4 = Capacitor [package=cap-pth-small2]
  Y2 = CRYSTAL [package=crystal-smd-10.5x4.8-2pin]
  J4 = Piezo Speaker

nets:
  N1: ArduinoKid.D9_PWM, C1.+, LED1.anode, A2.A0
  GND: ArduinoKid.GND, C1.-, R1.Pin_1, A2.GND, C3.2, C4.2, J4.pin1
  5V: ArduinoKid.5V, A2.VCC, A2.AVCC, A2.AREF
  N2: LED1.cathode, R1.Pin_0
  N3: A2.XLAT1, C3.1, Y2.1
  N4: A2.XLAT2, C4.1, Y2.2
  N5: A2.D12, J4.pin2

notes:
  Kid Arduino
  Observer
  The LED Trial Shield Blue belt
  Capacitor enables to detect PWM
  LED that student must control with PWM
