# Fritzing sketch LedTrialShieldWhiteBelt (saved by Fritzing 0.8.7b)
circuit board: 8cm x 10cm
breadboards: 2

parts:
  ArduinoStudent = Arduino Uno (Rev3)
  LED1 = LED - 5mm [color="Red (633nm)" package="5 mm [THT]"]
  R1 = Resistor [tolerance=±5% resistance=220 package=THT]
  J6 = Piezo Speaker
  C7 = Capacitor [package=cap-pth-small2]
  C8 = Capacitor [package=cap-pth-small2]
  Y4 = CRYSTAL [package=crystal-smd-10.5x4.8-2pin]
  A5 = atmega328 [package=dip]

nets:
  N1: ArduinoStudent.D13/SCK, LED1.anode, A5.A0
  GND: ArduinoStudent.GND, R1.Pin_1, J6.pin1, C7.2, C8.2, A5.GND
  5V: ArduinoStudent.5V, A5.VCC, A5.AVCC, A5.AREF
  N2: LED1.cathode, R1.Pin_0
  N3: J6.pin2, A5.D12
  N4: C7.1, Y4.1, A5.XLAT1
  N5: C8.1, Y4.2, A5.XLAT2

notes:
  Observer
  The LED Trial Shield White belt
