# Fritzing sketch LedTrialShieldYellowBelt (saved by Fritzing 0.8.7b)
circuit board: 8cm x 10cm
breadboards: 2

parts:
  ArduinoStudent = Arduino Uno (Rev3)
  LED1 = LED - 5mm [color="Red (633nm)" package="5 mm [THT]"]
  LED2 = LED - 5mm [color="Red (633nm)" package="5 mm [THT]"]
  R2 = Resistor [tolerance=±5% resistance=220 package=THT]
  R1 = Resistor [tolerance=±5% resistance=220 package=THT]
  J6 = Piezo Speaker
  A4 = atmega328 [package=dip]
  C7 = Capacitor [package=cap-pth-small2]
  C8 = Capacitor [package=cap-pth-small2]
  Y4 = CRYSTAL [package=crystal-smd-10.5x4.8-2pin]

nets:
  N1: ArduinoStudent.D12/MISO, LED2.anode, A4.A1
  N2: ArduinoStudent.D13/SCK, LED1.anode, A4.A0
  GND: ArduinoStudent.GND, R2.Pin_1, R1.Pin_1, J6.pin1, A4.GND, C7.2, C8.2
  5V: ArduinoStudent.5V, A4.VCC, A4.AVCC, A4.AREF
  N3: LED1.cathode, R1.Pin_0
  N4: LED2.cathode, R2.Pin_0
  N5: J6.pin2, A4.D12
  N6: A4.XLAT1, C7.1, Y4.1
  N7: A4.XLAT2, C8.1, Y4.2

notes:
  Observer
  The LED Trial Shield Yellow belt
